// Logisim project HW4_1.circ as structural Verilog: 1 circuit, main circuit main
module main (
  input  [1:0] inputA,
  input  [1:0] inputB,
  input  inputC,
  output [1:0] outputR,
  output outputQ
);

  wire and_3_out, and_4_out, and_5_out, c1, g0, g1, p0, p1;

  and and_1 (g0, inputA[0], inputB[0]);
  xor xor_1 (p0, inputA[0], inputB[0]);
  and and_2 (g1, inputA[1], inputB[1]);
  xor xor_2 (p1, inputA[1], inputB[1]);
  and and_3 (and_3_out, inputC, p0);
  and and_4 (and_4_out, inputC, p0, p1);
  and and_5 (and_5_out, g0, p1);
  or or_1 (c1, g0, and_3_out);
  or or_2 (outputQ, and_4_out, and_5_out, g1);
  xor xor_3 (outputR[0], inputC, p0);
  xor xor_4 (outputR[1], c1, p1);

  // Other names for the same wires on the sheet: c0 = inputC; c2 = outputQ; a0 = inputA[0]; a1 = inputA[1];
  //   b0 = inputB[0]; b1 = inputB[1]; r0 = outputR[0]; r1 = outputR[1]
endmodule
