// Logisim project HW4_2.circ as structural Verilog: 1 circuit, main circuit main
module main (
  input  in_1,
  output [2:0] O
);

  wire and_1_out, and_2_out, and_3_out, and_4_out, clock_1_out, not_1_out, not_2_out, not_3_out, or_1_out,
       or_2_out;

  not not_1 (not_1_out, O[2]);
  not not_2 (not_2_out, O[1]);
  not not_3 (not_3_out, O[0]);
  and and_1 (and_1_out, O[1], O[0]);
  and and_2 (and_2_out, O[2], not_3_out);
  and and_3 (and_3_out, not_1_out, not_2_out, O[0]);
  and and_4 (and_4_out, O[1], not_3_out);
  or or_1 (or_1_out, and_1_out, and_2_out);
  or or_2 (or_2_out, and_3_out, and_4_out);
  Clock clock_1 (.out(clock_1_out));
  Register #(.width(1)) bit2 (.D(or_1_out), .clk(clock_1_out), .Q(O[2]), .clr(in_1));  // open: en
  Register #(.width(1)) bit1 (.D(or_2_out), .clk(clock_1_out), .Q(O[1]), .clr(in_1));  // open: en
  Register #(.width(1)) bit0 (.D(not_3_out), .clk(clock_1_out), .Q(O[0]), .clr(in_1));  // open: en
endmodule
