// Logisim project ex3.circ as structural Verilog: 1 circuit, main circuit AddMachine
module AddMachine (
  output halt,
  output [7:0] ADD_OUT,
  output [7:0] REG_OUT
);

  wire clock_1_out;

  Comparator comparator_1 (.a(REG_OUT), .b({8{1'b1}}), .eq(halt));  // open: gt, lt
  Adder adder_1 (.a(8'h1), .b(REG_OUT), .out(ADD_OUT));  // open: cin, cout
  Register register_1 (.D(ADD_OUT), .clk(clock_1_out), .Q(REG_OUT));  // open: en, clr
  Clock clock_1 (.out(clock_1_out));

  // Notes on the sheet:
  //   PUT CIRCUITRY HERE
endmodule
