// Logisim project ex2_test.circ as structural Verilog: 1 circuit, main circuit main
module main (
  output [7:0] out_1,
  output NAND_OUT,
  output halt,
  output NOR_OUT,
  output XOR_OUT,
  output MUX2_OUT,
  output MUX4_OUT,
  output HA_SUM,
  output HA_CARRY,
  output out_10,
  output out_11,
  output out_12,
  output out_13,
  output out_14,
  output out_15
);

  wire clock_1_out;
  wire [7:0] adder_1_out;

  Register register_1 (.D(adder_1_out), .clk(clock_1_out), .Q(out_1));  // open: en, clr
  Clock clock_1 (.out(clock_1_out));
  Adder adder_1 (.a(8'h1), .b(out_1), .out(adder_1_out));  // open: cin, cout
  ROM #(.dataWidth(1)) rom_1 (.addr(out_1));  // open: data
  ROM #(.dataWidth(1)) rom_2 (.addr(out_1));  // open: data
  Comparator comparator_1 (.a(out_1), .b(8'h10), .eq(halt));  // open: gt, lt
  ROM #(.dataWidth(1)) rom_3 (.addr(out_1));  // open: data
  ROM #(.dataWidth(1)) rom_4 (.addr(out_1));  // open: data
  NAND1 nand1_1 (.A(out_10), .B(out_11), .RESULT(NAND_OUT));
  NOR1 nor1_1 (.A(out_10), .B(out_11), .RESULT(NOR_OUT));
  XOR1 xor1_1 (.A(out_10), .B(out_11), .RESULT(XOR_OUT));
  MUX2 mux2_1 (.A(out_10), .B(out_11), .Sel(out_14), .RESULT(MUX2_OUT));
  MUX4 mux4_1 (.A(out_10), .B(out_11), .C(out_12), .D(out_13), .Sel1(out_14), .Sel2(out_15), .RESULT(MUX4_OUT));
  Half_Adder half_adder_1 (.A(out_10), .B(out_11), .SUM(HA_SUM), .CARRY(HA_CARRY));
  ROM #(.dataWidth(1)) rom_5 (.addr(out_1));  // open: data
  ROM #(.dataWidth(1)) rom_6 (.addr(out_1));  // open: data

  // Other names for the same wires on the sheet: A = out_10; B = out_11; C = out_12; D = out_13; Sel1 = out_14;
  //   Sel2 = out_15; Test[7:0] = out_1

  // Notes on the sheet:
  //   contents of rom_1 (hex, n*v repeats v):
  //   0 0 1 1 34*0 1 11*0 1 0 1 0 0 0 1 141*0 1 19*0 1
  //   contents of rom_2 (hex, n*v repeats v):
  //   6*1
  //   contents of rom_3 (hex, n*v repeats v):
  //   0 1 0 1 0 0 1 4*0 1 7*0 1 63*0 1 0 0 1 46*0 1
  //   contents of rom_4 (hex, n*v repeats v):
  //   0 1 0 1
  //   contents of rom_5 (hex, n*v repeats v):
  //   1 0 1 1 0 0 1 0 0 1
  //   contents of rom_6 (hex, n*v repeats v):
  //   0 1 1
endmodule
